# Fritzing sketch Schematic_Board (saved by Fritzing 0.9.6b)
perfboards: 1

parts:
  OLED_I2C1 = OLED 128x64 I2C Monochrome Display  # not connected
  S1 = Toggle Switch [package=THT]  # not connected
  A3 = ESP32-S3 supermini  # not connected
  J1 = female pin header, 9 pins [form="♀ (female)"]
  J3 = male pin header, 9 pins [form="♂ (male)"]
  S33 = Momentary Switch 6mm 2pin
  S34 = Momentary Switch 6mm 2pin
  S35 = Momentary Switch 6mm 2pin
  S36 = Momentary Switch 6mm 2pin
  S37 = Momentary Switch 6mm 2pin
  S38 = Momentary Switch 6mm 2pin
  S39 = Momentary Switch 6mm 2pin
  S40 = Momentary Switch 6mm 2pin
  S41 = Momentary Switch 6mm 2pin
  S42 = Momentary Switch 6mm 2pin
  S43 = Momentary Switch 6mm 2pin
  S44 = Momentary Switch 6mm 2pin
  S45 = Momentary Switch 6mm 2pin
  S46 = Momentary Switch 6mm 2pin
  S47 = Momentary Switch 6mm 2pin
  S48 = Momentary Switch 6mm 2pin
  J4 = male pin header, 9 pins [form="♂ (male)"]
  J6 = Generic male header - 5 pins [form="♂ (male)" package=THT]
  J7 = male pin header, 4 pins [form="♂ (male)"]  # not connected
  R1 = Resistor [tolerance=±5% resistance=120k package="2010 [SMD]"]  # not connected

nets:
  N1: J1.pin1, J3.pin1
  N2: J1.pin2, J3.pin2
  N3: J1.pin3, J3.pin3
  N4: J1.pin4, J3.pin4
  N5: J1.pin5, J3.pin5
  N6: J1.pin6, J3.pin6
  N7: J1.pin7, J3.pin7
  N8: J1.pin8, J3.pin8
  N9: J1.pin9, J3.pin9, S33.2, S37.2, S41.2, S45.2
  N10: S33.1, S34.1, S35.1, S36.1
  N11: S34.2, S39.2, S43.2, S47.2
  N12: S35.2, S40.2, S44.2, S48.2
  N13: S36.2, S38.2, S42.2, S46.2
  N14: S37.1, S38.1, S39.1, S40.1
  N15: S41.1, S42.1, S43.1, S44.1
  N16: S45.1, S46.1, S47.1, S48.1
  N17: J4.pin3, J6.pin3
  N18: J4.pin4, J6.pin4
  N19: J4.pin5, J6.pin5

custom parts:
  ESP32-S3 supermini: Esp32-S3 Development board ESP32 SuperMini development board ESP32 Development board WiFi Bluetooth.
  Momentary Switch 6mm 2pin: Momentary Switch 6mm 2 pin Button commonly used for reset or general input.
  Generic male header - 5 pins: Generic male header
